# Fritzing sketch Solar Panel Cleaner Schematic (saved by Fritzing 0.9.3b)
breadboards: 1

parts:
  Part1 = Arduino Mega ADK (Rev3)
  hc-sr1 = hc-sr04
  hc-sr3 = hc-sr04
  hc-sr4 = hc-sr04
  Part2 = Real Time Clock Module - DS1307 RTC Breakout Board
  Part3 = ACS712 Low Current Sensor Board v12
  Mod1 = Voltage Sensor 25V
  M1 = BTS7960
  LCD1 = 20x4 LCD display [part_number=2004A]
  U1 = Mini-360 DC-DC Buck converter [package=THT]
  M2 = DC Motor
  M3 = DC Motor
  M4 = DC Motor
  U2 = 2-Channel 5v Relay Shield [package=relay-2ch5v10a]
  M5 = BTS7960
  Part4 = Solar Panel [package="Renogy 50 Watts 12 Volt Monocrystalline Bendable Solar Panel"]
  Part5 = Solar Charge Controller [part_number="HGX Series Solar Charge Controller PWM" package=PWM-Model]
  BAT1 = 12 battery [package=battery]
  LED1 = LEDs [package=led10mm]
  X1 = USB Connectors [package=usb-b-pth]
  R1 = Resistor [tolerance=±5% resistance=220 package="0402 [SMD]"]
  U4 = POT [package=trim_pot]

nets:
  N1: Part1.A0, Mod1.S
  N2: Part1.A1, Part3.VO
  N3: Part1.D21/SCL, Part2.SCL
  N4: Part1.D20/SDA, Part2.SDA
  N5: Part1.D2_PWM, M1.pin1
  N6: Part1.D3_PWM, M1.pin2
  N7: Part1.D4_PWM, M5.pin1
  N8: Part1.D5_PWM, M5.pin2
  N9: Part1.D22, M1.pin3
  N10: Part1.D23, M1.pin4
  N11: Part1.D24, M5.pin3
  N12: Part1.D25, M5.pin4
  N13: Part1.D26, hc-sr4.Trig
  N14: Part1.D27, hc-sr4.Echo
  N15: Part1.D28, hc-sr3.Trig
  N16: Part1.D29, hc-sr3.Echo
  N17: Part1.D30, hc-sr1.Trig
  N18: Part1.D31, hc-sr1.Echo
  N19: Part1.D35, LCD1.DB7
  N20: Part1.D36, U2.IN2
  N21: Part1.D37, LCD1.DB6
  N22: Part1.D38, U2.IN1
  N23: Part1.D39, LCD1.DB5
  N24: Part1.D41, LCD1.DB4
  N25: Part1.D43, LCD1.RS
  N26: Part1.D45, LCD1.E
  VCC: hc-sr3.VCC, hc-sr4.VCC
  GND: hc-sr3.GND, hc-sr4.GND
  GND_2: Part3.GND, Mod1.GND, Mod1.-
  N27: M1.pin7, M5.pin7
  N28: M1.pin8, M5.pin8
  N29: M1.pin9, M3.pin_2
  N30: M1.pin10, M3.pin_1
  N31: LCD1.Vss, LCD1.K_-, U4.S
  N32: LCD1.Vdd, R1.Pin_1, U4.A
  N33: LCD1.Vo, U4.E
  N34: LCD1.A_+, R1.Pin_0
  N35: U1.OUT+, X1.VBUS
  N36: U1.OUT-, X1.GND
  N37: M2.pin_2, U2.K2-On
  N38: M4.pin_1, M5.pin10
  N39: M4.pin_2, M5.pin9
  N40: Part4.Connector_1, Part5.Connector_1
  N41: Part4.Connector_2, Part5.Connector_2
  N42: Part5.Connector_3, BAT1.+
  N43: Part5.Connector_4, BAT1.-
  N44: Part5.Connector_5, LED1.A
  N45: Part5.Connector_6, LED1.C

notes:
  DC 12V Water Pump

custom parts:
  BTS7960: BTS7960 43A Peak Power H-Bridge PWM Motor Driver
  20x4 LCD display: 20x4 character display. CHECK LED POLARITY BEFORE CONNECTING POWER Some versions of the dispaly have the polarity of the LED pins "A" and "K" reversed.
  Mini-360 DC-DC Buck converter: Mini-360 DC-DC Buck converter. Tiny buck step down voltage converter, input voltage 4.75 to 23V output 1 to 17V adjustable. Available from ebay and the like.
  2-Channel 5v Relay Shield: 2 Channel 5v Relay Shield w. 2x SPD-06VDC-SD-C
  Solar Panel: Renogy 50 Watts 12 Volt Solar Panel
  Solar Charge Controller: PWM-Solar Charge Controller
  12 battery: 12V lead acid type battery, like the Husqvarna YTH2448 12V 35AH battery. This is the mini version 1/4 the size of the actual battery to be closer to typical breadboard parts (around 2in wide rathher than 7in). The pads in pcb are sized to accomidate up to 14ga wire (as these batterys will deliver high currents.)
  LEDs: LEDs Standard schematic elements and footprints for 5mm, 3mm, 1206, and 0603 sized LEDs. 5mm - Spark Fun Electronics SKU : COM-00529 (and others)
